# Fritzing sketch sketch_ESP8266 (saved by Fritzing 0.9.3b)
breadboards: 1

parts:
  U1 = ESP8266 WiFi Module [part_number=ESP8266]
  Part1 = Arduino Uno (Rev3) - ICSP
  U2 = Voltage Regulator [package=to220-adj]

nets:
  N1: U1.RXD, Part1.D0/RX
  N2: U1.VCC, U1.CH_PD, U2.ADJ
  GND: U1.GPIO_0, U1.GND, Part1.GND, U2.OUT
  N3: U1.TXD, Part1.D1/TX
  N4: Part1.5V, U2.IN

custom parts:
  ESP8266 WiFi Module: Generic WiFi Module based on the ESP8266 with onboard PCB antenna and UART communications
